# Fritzing sketch test17Stepper (saved by Fritzing 0.9.3b)
breadboards: 1

parts:
  부품2 = Arduino Uno (Rev3)
  M2 = Stepper Motor - Unipolar
  ULN2003A_-_Stepper_Driver_Board1 = ULN2003A - Stepper Driver Board [package=board]

nets:
  N1: 부품2.D8, ULN2003A_-_Stepper_Driver_Board1.IN1
  N2: 부품2.D9_PWM, ULN2003A_-_Stepper_Driver_Board1.IN2
  N3: 부품2.D10_PWM/SS, ULN2003A_-_Stepper_Driver_Board1.IN3
  N4: 부품2.D11_PWM/MOSI, ULN2003A_-_Stepper_Driver_Board1.IN4
  5V: 부품2.5V, ULN2003A_-_Stepper_Driver_Board1.VCC
  GND: 부품2.GND, ULN2003A_-_Stepper_Driver_Board1.GND
  N5: M2.A, M2.COMMON_1, ULN2003A_-_Stepper_Driver_Board1.BLUE
  N6: M2.C, ULN2003A_-_Stepper_Driver_Board1.PINK
  N7: M2.B, ULN2003A_-_Stepper_Driver_Board1.YELLOW
  N8: M2.COMMON_2, ULN2003A_-_Stepper_Driver_Board1.ORANGE
  N9: M2.D, ULN2003A_-_Stepper_Driver_Board1.RED

custom parts:
  ULN2003A - Stepper Driver Board: A common stepper motor driver board based on ULN2003APG darlington array
