# Fritzing sketch test18Joystick_stepper (saved by Fritzing 0.9.3b)
breadboards: 1

parts:
  부품2 = Arduino Uno (Rev3)
  M2 = Stepper Motor - Unipolar
  ULN2003A_-_Stepper_Driver_Board1 = ULN2003A - Stepper Driver Board [package=board]
  부품3 = Thumb Joystick

nets:
  N1: 부품2.A0, 부품3.VERT
  N2: 부품2.A1, 부품3.HORZ
  N3: 부품2.D8, ULN2003A_-_Stepper_Driver_Board1.IN1
  N4: 부품2.D9_PWM, ULN2003A_-_Stepper_Driver_Board1.IN2
  N5: 부품2.D10_PWM/SS, ULN2003A_-_Stepper_Driver_Board1.IN3
  N6: 부품2.D11_PWM/MOSI, ULN2003A_-_Stepper_Driver_Board1.IN4
  N7: 부품2.D4, 부품3.SEL
  VCC: 부품2.5V, ULN2003A_-_Stepper_Driver_Board1.VCC, 부품3.VCC
  GND: 부품2.GND, ULN2003A_-_Stepper_Driver_Board1.GND, 부품3.GND
  N8: M2.A, M2.COMMON_1, ULN2003A_-_Stepper_Driver_Board1.BLUE
  N9: M2.C, ULN2003A_-_Stepper_Driver_Board1.PINK
  N10: M2.B, ULN2003A_-_Stepper_Driver_Board1.YELLOW
  N11: M2.COMMON_2, ULN2003A_-_Stepper_Driver_Board1.ORANGE
  N12: M2.D, ULN2003A_-_Stepper_Driver_Board1.RED

custom parts:
  ULN2003A - Stepper Driver Board: A common stepper motor driver board based on ULN2003APG darlington array
